# Fritzing sketch medidaTemperatura (saved by Fritzing 0.9.1b)
breadboards: 1

parts:
  T1 = LM35 Temperature Sensor [package="TO92 [THT]"]
  Parte1 = Arduino Uno (Rev3)
  RE1 = Rotary Encoder [package=THT]
  LCD1 = LCD screen
  R1 = Resistor [tolerance=±5% resistance=220 package=THT]

nets:
  5V: T1.+Vs, Parte1.5V, RE1.EncoderPinA, LCD1.VDD, R1.Pin_0
  N1: T1.Vout, Parte1.A0
  GND: T1.GND, Parte1.GND, RE1.EncoderPinB, LCD1.VSS, LCD1.LED-
  N2: Parte1.D11_PWM/MOSI, LCD1.E
  N3: Parte1.D12/MISO, LCD1.RS
  N4: Parte1.D2, LCD1.DB7
  N5: Parte1.D3_PWM, LCD1.DB6
  N6: Parte1.D4, LCD1.DB5
  N7: Parte1.D5_PWM, LCD1.DB4
  N8: RE1.EncoderPinC, LCD1.V0
  N9: LCD1.LED+, R1.Pin_1
