# Fritzing sketch dadoElectronico (saved by Fritzing 0.9.1b)
breadboards: 1

parts:
  Parte1 = Arduino Uno (Rev3)
  LED2 = LED - 5mm [color="Red (633nm)" package="5 mm [THT]"]
  LED3 = LED - 5mm [color="Red (633nm)" package="5 mm [THT]"]
  LED4 = LED - 5mm [color="Red (633nm)" package="5 mm [THT]"]
  LED5 = LED - 5mm [color="Red (633nm)" package="5 mm [THT]"]
  LED6 = LED - 5mm [color="Red (633nm)" package="5 mm [THT]"]
  LED7 = LED - 5mm [color="Red (633nm)" package="5 mm [THT]"]
  R1 = Resistor [tolerance=±5% resistance=220 package=THT]
  R2 = Resistor [tolerance=±5% resistance=220 package=THT]
  R3 = Resistor [tolerance=±5% resistance=220 package=THT]
  R4 = Resistor [tolerance=±5% resistance=220 package=THT]
  R5 = Resistor [tolerance=±5% resistance=220 package=THT]
  R6 = Resistor [tolerance=±5% resistance=220 package=THT]
  R7 = Resistor [tolerance=±5% resistance=220 package=THT]
  LED8 = LED - 5mm [color="Red (633nm)" package="5 mm [THT]"]
  S1 = Pushbutton [package="[THT]"]
  R8 = Resistor [tolerance=±5% resistance=1k package=THT]

nets:
  N1: Parte1.D8, LED4.anode
  N2: Parte1.D1/TX, LED7.anode
  N3: Parte1.D2, S1.Pin_1, S1.Pin_2, R8.Pin_0
  N4: Parte1.D3_PWM, LED6.anode
  N5: Parte1.D4, LED5.anode
  N6: Parte1.D5_PWM, LED8.anode
  N7: Parte1.D6_PWM, LED2.anode
  N8: Parte1.D7, LED3.anode
  N9: Parte1.5V, S1.Pin_3, S1.Pin_4
  N10: Parte1.GND, R1.Pin_1, R2.Pin_1, R3.Pin_1, R4.Pin_0, R5.Pin_1, R6.Pin_1, R7.Pin_1, R8.Pin_1
  N11: LED2.cathode, R3.Pin_0
  N12: LED3.cathode, R2.Pin_0
  N13: LED4.cathode, R1.Pin_0
  N14: LED5.cathode, R5.Pin_0
  N15: LED6.cathode, R4.Pin_1
  N16: LED7.cathode, R6.Pin_0
  N17: R7.Pin_0, LED8.cathode
