# Fritzing sketch reproductor (saved by Fritzing 0.9.1b)
breadboards: 1

parts:
  Parte1 = Arduino Uno (Rev3)
  S1 = Pushbutton [package="[THT]"]
  J1 = Piezo Speaker
  R1 = Rotary Potentiometer (Small) [maximum_resistance=100kΩ package=THT]
  R2 = Resistor [tolerance=±5% resistance=1k package=THT]

nets:
  N1: Parte1.D2, S1.Pin_1, S1.Pin_2, R2.Pin_0
  N2: Parte1.D3_PWM, R1.leg2
  N3: Parte1.5V, S1.Pin_3, S1.Pin_4
  N4: Parte1.GND, J1.pin1, R2.Pin_1
  N5: J1.pin2, R1.leg1, R1.wiper
